# Fritzing sketch wiring (saved by Fritzing 0.9.6b)
circuit board: 2.84924cm x 3.73642cm
breadboards: 1

parts:
  R4 = Resistor [tolerance=±5% power=0.25W resistance=1k package=THT]
  R2 = Resistor [tolerance=±5% power=0.25W resistance=100 package=THT]
  Q1 = PNP-Transistor [mpn=2N3906 package="TO92 [THT]"]
  R1 = Resistor [tolerance=±5% power=0.25W resistance=47k package=THT]
  R3 = Resistor [tolerance=±5% power=0.25W resistance=4.7k package=THT]
  J1 = male pin header, 3 pins [form="♂ (male)"]
  J2 = male pin header, 2 pins [form="♂ (male)"]
  J3 = male pin header, 2 pins [form="♂ (male)"]
  Q2 = NPN-Transistor [part_number=2N3904 package="TO92 [THT]"]
  R5 = Resistor [tolerance=±5% power=0.25 resistance=1k package=THT]
  J4 = male pin header, 1 pin [form="♂ (male)"]
  C1 = Tantalum Capacitor [capacitance=22µF voltage=6V part_number=6300mF package="100 mil [THT, tantalum]"]

nets:
  N1: R4.Pin_0, J2.pin1
  N2: R4.Pin_1, Q2.B
  N3: R2.Pin_0, Q1.B, R1.Pin_1
  N4: R2.Pin_1, Q2.C
  N5: Q1.E, R1.Pin_0, J3.pin1, C1.+
  N6: Q1.C, R3.Pin_0, J1.pin2
  N7: R3.Pin_1, J1.pin1, J2.pin2
  GND: J1.pin3, J3.pin2, Q2.E, R5.Pin_1, C1.-
  N8: R5.Pin_0, J4.pin1
